# Fritzing sketch sea (saved by Fritzing 0.9.3b)
breadboards: 1

parts:
  Part1 = Arduino Uno (Rev3)
  IC1 = L293D [package=THT]
  IC2 = L293D [package=THT]
  M1 = DC Motor
  M2 = DC Motor
  M3 = DC Motor
  S2 = Square Pushbutton
  S3 = Square Pushbutton
  U2 = JOYSTICK-PSP1000 [package=joystick-psp1000]

nets:
  N1: Part1.A0, U2.X
  N2: Part1.A1, U2.Y
  N3: Part1.A2, S3.leg1
  N4: Part1.A3, S2.leg1
  N5: Part1.D8, IC1.In_1
  N6: Part1.D9_PWM, IC1.In_2
  N7: Part1.D10_PWM/SS, IC1.In_3
  N8: Part1.D11_PWM/MOSI, IC1.In_4
  N9: Part1.D12/MISO, IC2.In_1
  N10: Part1.D13/SCK, IC2.In_2
  GND: Part1.GND, IC1.0V, IC2.0V, U2.GND
  N11: Part1.D3_PWM, IC2.Enable_1
  N12: Part1.D5_PWM, IC1.Enable_1
  N13: Part1.D6_PWM, IC1.Enable_2
  5V: Part1.5V, IC1.+V, S2.leg0, S3.leg0, U2.VCC
  N14: IC1.Out_1_(_Controlled_by_Enable_1_), M1.pin_2
  N15: IC1.Out_2_(_Controlled_by_Enable_1_), M1.pin_1
  N16: IC1.Out_3_(_Controlled_by_Enable_2_), M2.pin_2
  N17: IC1.Out_4_(_Controlled_by_Enable_2_), M2.pin_1
  N18: IC2.Out_1_(_Controlled_by_Enable_1_), M3.pin_2
  N19: IC2.Out_2_(_Controlled_by_Enable_1_), M3.pin_1
